# Fritzing sketch GoPro Timelapse (saved by Fritzing 0.9.3b)
circuit board: 8.46667cm x 5.64444cm
breadboards: 1

parts:
  Part1 = Arduino Uno (Rev3)
  BLUETOOTH_MODULE = Bluetooth HC-05 Macho
  GREENLED = smd LED [color="Red (633nm)" package="0805 [SMD]"]
  PIEZO = Piezo Speaker
  REDLED = smd LED [color="Red (633nm)" package="0805 [SMD]"]
  SERVO = Basic Servo
  R2 = Resistor [tolerance=±5% resistance=220 package=THT]
  R1 = Resistor [tolerance=±5% resistance=220 package=THT]

nets:
  N1: Part1.D10_PWM/SS, BLUETOOTH_MODULE.RXD
  N2: Part1.D11_PWM/MOSI, BLUETOOTH_MODULE.TXD
  N3: Part1.D12/MISO, R1.Pin_1
  N4: Part1.D13/SCK, R2.Pin_0
  GND: Part1.GND, BLUETOOTH_MODULE.GND, GREENLED.cathode, PIEZO.pin1, REDLED.cathode, SERVO.gnd
  N5: Part1.D3_PWM, PIEZO.pin2
  N6: Part1.D5_PWM, SERVO.pulse
  VCC: Part1.5V, BLUETOOTH_MODULE.VCC, SERVO.vcc
  N7: GREENLED.anode, R1.Pin_0
  N8: REDLED.anode, R2.Pin_1
