# Fritzing sketch GoPro Timelapse (saved by Fritzing 0.9.3b)
circuit board: 8.46667cm x 5.64444cm
breadboards: 1

parts:
  Part1 = Arduino Uno (Rev3)
  BLUETOOTH_MODULE = Bluetooth HC-05 Macho
  GREENLED = smd LED [color="Red (633nm)" package="0805 [SMD]"]
  PIEZO = Piezo Speaker
  REDLED = smd LED [color="Red (633nm)" package="0805 [SMD]"]
  SERVO = Basic Servo
  R2 = Resistor [tolerance=±5% resistance=220 package=THT]
  R1 = Resistor [tolerance=±5% resistance=220 package=THT]

nets:
  N1: Part1.D10_PWM/SS, BLUETOOTH_MODULE.RXD
  N2: Part1.D11_PWM/MOSI, BLUETOOTH_MODULE.TXD
  N3: Part1.D12/MISO, R1.Pin_1
  N4: Part1.D13/SCK, R2.Pin_0
  GND: Part1.GND, BLUETOOTH_MODULE.GND, GREENLED.cathode, PIEZO.pin1, REDLED.cathode, SERVO.gnd
  N5: Part1.D3_PWM, PIEZO.pin2
  N6: Part1.D5_PWM, SERVO.pulse
  VCC: Part1.5V, BLUETOOTH_MODULE.VCC, SERVO.vcc
  N7: GREENLED.anode, R1.Pin_0
  N8: REDLED.anode, R2.Pin_1

// code stored in the sketch: Untitled2.ino
// some parts taken from http://www.genotronex.com/
#include <SoftwareSerial.h>// import the serial library
#include <Servo.h>
Servo myservo;// values 0-180
SoftwareSerial Genotronex(11, 10); // RX, TX
int redledpin=13;
int greenledpin = 12;
int BluetoothData; // the data given from Computer
int buzzerPin = 3;

void setup() {
  // put your setup code here, to run once:
  Genotronex.begin(9600);
  Genotronex.println("Bluetooth On");
  pinMode(redledpin,OUTPUT);
  myservo.attach(5); //set pin 5 as the servo pin
  pinMode(buzzerPin, OUTPUT);
  pinMode(greenledpin, OUTPUT);
}

void loop() {
  digitalWrite(greenledpin,HIGH);
  // put your main code here, to run repeatedly:
   if (Genotronex.available())
   {
      BluetoothData=Genotronex.read(); //read data that's sent via bluetooth
      
      digitalWrite(greenledpin,HIGH); //light up green led to signal waiting for a command
      if (BluetoothData=='1')
      {
        //beeping noise
        analogWrite(buzzerPin, 20);  
        delay(1000);
        analogWrite(buzzerPin, 0);
        
        digitalWrite(greenledpin,LOW); //turn off green led
        
        for(int i=1000;i<=2000;i++) //angle when at 0 degrees is 1000 and at 180 is 2000
          {
             digitalWrite(redledpin,HIGH); //red led blinking
             myservo.writeMicroseconds(i); // move at desired angle
             delay(500); //wait till camera takes picture
             digitalWrite(redledpin,LOW); //red led blinking
             digitalWrite(greenledpin,0);
             delay(500);
          }
      }
      if (BluetoothData=='2')
      {
        //beeping noise
        analogWrite(buzzerPin, 20);  
        delay(1000);
        analogWrite(buzzerPin, 0);
        
        digitalWrite(greenledpin,LOW);//turn off green led
        
        for(int i=1000;i<=2000;i++)//angle when at 0 degrees is 1000 and at 180 is 2000
          {
             digitalWrite(redledpin,HIGH);//red led blinking
             myservo.writeMicroseconds(i);// move at desired angle
             delay(1000);//wait till camera takes picture
             digitalWrite(redledpin,LOW);//red led blinking
             digitalWrite(greenledpin,0);//turn off green led
             delay(1000);
          }
      }
      if (BluetoothData=='5')
      {
        //beeping noise
        analogWrite(buzzerPin, 20);  
        delay(1000);
        analogWrite(buzzerPin, 0);
        
        digitalWrite(greenledpin,LOW);//turn off green led
        
        for(int i=1000;i<=2000;i++)//angle when at 0 degrees is 1000 and at 180 is 2000
          {
             digitalWrite(redledpin,HIGH);//red led blinking
             myservo.writeMicroseconds(i);// move at desired angle
             delay(2500);//wait till camera takes picture
             digitalWrite(redledpin,LOW);//red led blinking
             digitalWrite(greenledpin,0);//turn off green led
             delay(2500);
          }
      }
    }
    delay(100);// prepare for next data
}
